# Fritzing sketch wiring-h-bridge (saved by Fritzing 0.8.5b)

parts:
  M1 = DC Motor
  U1 = RELAY [package=relay-g5q]
  U2 = RELAY [package=relay-g5q]
  S1 = Pushbutton [package="[THT]"]  # not connected
  S2 = Pushbutton [package="[THT]"]  # not connected
  S3 = Pushbutton [package="[THT]"]  # not connected
  S4 = Pushbutton [package="[THT]"]  # not connected
  J1 = screw terminal, 9 pins
  R1 = Resistor [package="2010 [SMD]"]
  LED1 = smd LED [color="Red (633nm)" package="0603 [SMD]"]
  U3 = LIPO-1000mAh [package=lipo-1000]

nets:
  N1: M1.pin_1, U1.MAIN
  N2: M1.pin_2, U2.MAIN
  N3: U1.COIL2, U2.COIL2, U3.-
  N4: U1.NO, U2.NO, U3.+
  N5: J1.pin1, R1.Pin_0
  N6: J1.pin9, LED1.cathode
  N7: R1.Pin_1, LED1.anode

notes:
  Relays in H-bridge
  Digital outputs
  5v then IO 0-7
  Input 0: reverse
  Input 1: forward
  Input 2: reboot
  Input 3: halt
